// Logisim project ETFStudent.circ as structural Verilog: 3 circuits, main circuit KMADR
module KMADR (
  input  immed,
  input  memdir,
  input  memind,
  input  regind,
  input  postincr,
  input  postdec,
  input  regdir,
  output [4:0] Adr
);

  assign Adr = immed ? 5'b00010 : 5'bz;  // Controlled_Buffer controlled_buffer_1
  assign Adr = memdir ? 5'b00100 : 5'bz;  // Controlled_Buffer controlled_buffer_2
  assign Adr = memind ? 5'b00101 : 5'bz;  // Controlled_Buffer controlled_buffer_3
  assign Adr = regind ? 5'b01010 : 5'bz;  // Controlled_Buffer controlled_buffer_4
  assign Adr = postincr ? 5'b01011 : 5'bz;  // Controlled_Buffer controlled_buffer_5
  assign Adr = postdec ? 5'b01100 : 5'bz;  // Controlled_Buffer controlled_buffer_6
  assign Adr = regdir ? 5'b10010 : 5'bz;  // Controlled_Buffer controlled_buffer_7
endmodule

module KMOPR (
  input  LD,
  input  ST,
  input  ADD,
  input  SUB,
  input  BLSS,
  input  JLEQ,
  input  JMP,
  input  JSR,
  input  RTS,
  input  RTI,
  input  HALT,
  output [5:0] Adr5_0_c5f65dcb
);

  assign Adr5_0_c5f65dcb = LD ? 6'b000010 : 6'bz;  // Controlled_Buffer controlled_buffer_1
  assign Adr5_0_c5f65dcb = ST ? 6'b000100 : 6'bz;  // Controlled_Buffer controlled_buffer_2
  assign Adr5_0_c5f65dcb = ADD ? 6'b001010 : 6'bz;  // Controlled_Buffer controlled_buffer_3
  assign Adr5_0_c5f65dcb = SUB ? 6'b001100 : 6'bz;  // Controlled_Buffer controlled_buffer_4
  assign Adr5_0_c5f65dcb = BLSS ? 6'b001110 : 6'bz;  // Controlled_Buffer controlled_buffer_5
  assign Adr5_0_c5f65dcb = JLEQ ? 6'b010000 : 6'bz;  // Controlled_Buffer controlled_buffer_6
  assign Adr5_0_c5f65dcb = JMP ? 6'b010001 : 6'bz;  // Controlled_Buffer controlled_buffer_7
  assign Adr5_0_c5f65dcb = JSR ? 6'b010010 : 6'bz;  // Controlled_Buffer controlled_buffer_8
  assign Adr5_0_c5f65dcb = RTS ? 6'b010111 : 6'bz;  // Controlled_Buffer controlled_buffer_9
  assign Adr5_0_c5f65dcb = RTI ? 6'b011110 : 6'bz;  // Controlled_Buffer controlled_buffer_10
  assign Adr5_0_c5f65dcb = HALT ? 6'b100010 : 6'bz;  // Controlled_Buffer controlled_buffer_11
endmodule

module REG6_INC_LD (
  input  [5:0] I,
  input  LD,
  input  INC,
  input  mr,
  input  CLK,
  output [5:0] A
);

  wire reg2m_inc_ld_2_cout, reg2m_inc_ld_3_cout;

  REG2m_INC_LD reg2m_inc_ld_1 (
    .A(A[5:4]), .LD(LD), .Cin(reg2m_inc_ld_2_cout), .INC(INC), .mr(mr), .CLK(CLK), .I(I[5:4]));  // open: Cout
  REG2m_INC_LD reg2m_inc_ld_2 (
    .Cout(reg2m_inc_ld_2_cout), .A(A[3:2]), .LD(LD), .Cin(reg2m_inc_ld_3_cout), .INC(INC), .mr(mr),
    .CLK(CLK), .I(I[3:2]));
  REG2m_INC_LD reg2m_inc_ld_3 (
    .Cout(reg2m_inc_ld_3_cout), .A(A[1:0]), .LD(LD), .Cin(INC), .INC(INC), .mr(mr), .CLK(CLK), .I(I[1:0]));

  // Notes on the sheet:
  //   __
endmodule
